# Fritzing sketch pidrv8835stepper (saved by Fritzing 0.9.3b)

parts:
  Raspberry_Pi_1 = Raspberry Pi 3 [part_number=RPI-3-V1.2]  # not connected
  M3 = Stepper Motor - Bipolar
  Part1 = SparkFun_Qwiic_Motor_Driver
  JACK1 = 2.1mm Barrel Jack with Terminal Block

nets:
  N1: M3.A, Part1.BOUT2
  N2: M3.C, Part1.BOUT1
  N3: M3.B, Part1.AOUT2
  N4: M3.D, Part1.AOUT1
  N5: Part1.GND, JACK1.NEG
  N6: Part1.VIN, JACK1.POS
